# Fritzing sketch stimsync_pcb_electronic_brick (saved by Fritzing 0.8.0b)
breadboards: 1

parts:
  0v = female pin header, 14 pins [form="♀ (female)"]
  Teensy3 = female pin header, 14 pins [form="♀ (female)"]
  ThresholdA = Rotary Potentiometer (Small) [maximum_resistance=100kΩ part_number=potA]
  ThresholdB = Rotary Potentiometer (Small) [maximum_resistance=100kΩ part_number=potB]
  DetectA = LED - 5mm [color="Red (633nm)" part_number=LEDA package="5 mm [THT]"]
  DetectB = LED - 5mm [color="Red (633nm)" part_number=LEDB package="5 mm [THT]"]
  r220 = Resistor [tolerance=±5% resistance=220 package=THT]
  r220_2 = Resistor [tolerance=±5% resistance=220 package=THT]
  pot10K = female pin header, 1 pin [form="♀ (female)" part_number=PotLegA]  # not connected
  pot10k = female pin header, 1 pin [form="♀ (female)" part_number=PotLegB]  # not connected
  RF_(bottom) = female pin header, 4 pins [form="♀ (female)"]
  r140 = female pin header, 9 pins [form="♀ (female)"]
  Outputs = double row male pin header, 16 pins [form="♂ (male)"]
  Buttons = double row male pin header, 16 pins [form="♂ (male)"]
  0v_2 = female pin header, 2 pins [form="♀ (female)"]
  SensorA = female pin header, 3 pins [form="♀ (female)"]
  SensorB = female pin header, 3 pins [form="♀ (female)" part_number=A1-ElectronicBrickSensor]

nets:
  N1: 0v.pin1, Teensy3.pin2, ThresholdA.leg1, ThresholdB.leg1, DetectA.cathode, DetectB.cathode, RF_(bottom).pin2, r140.pin1, Buttons.pin1, Buttons.pin2, Buttons.pin3, Buttons.pin4, Buttons.pin5, Buttons.pin6, Buttons.pin7, Buttons.pin8, 0v_2.pin2, SensorA.pin1, SensorB.pin1
  N2: 0v.pin2, RF_(bottom).pin3
  N3: 0v.pin3, RF_(bottom).pin4
  N4: 0v.pin4, Buttons.pin16
  N5: 0v.pin5, Buttons.pin15
  N6: 0v.pin6, Buttons.pin14
  N7: 0v.pin7, Buttons.pin13
  N8: 0v.pin8, Buttons.pin12
  N9: 0v.pin9, Buttons.pin11
  N10: 0v.pin10, Buttons.pin10
  N11: 0v.pin11, Buttons.pin9
  N12: 0v.pin12, Outputs.pin16
  N13: 0v.pin13, Outputs.pin15
  N14: 0v.pin14, Outputs.pin14
  N15: Teensy3.pin1, RF_(bottom).pin1
  N16: Teensy3.pin3, ThresholdA.leg2, ThresholdB.leg2, 0v_2.pin1, SensorA.pin2, SensorB.pin2
  N17: Teensy3.pin4, Outputs.pin10
  N18: Teensy3.pin5, Outputs.pin11
  N19: Teensy3.pin6, Outputs.pin12
  N20: Teensy3.pin7, Outputs.pin13
  N21: Teensy3.pin8, r220_2.Pin_0
  N22: Teensy3.pin9, r220.Pin_0
  N23: Teensy3.pin10, ThresholdB.wiper
  N24: Teensy3.pin11, ThresholdA.wiper
  N25: Teensy3.pin12, SensorB.pin3
  N26: Teensy3.pin13, SensorA.pin3
  N27: Teensy3.pin14, Outputs.pin9
  N28: DetectA.anode, r220.Pin_1
  N29: DetectB.anode, r220_2.Pin_1
  N30: r140.pin2, Outputs.pin1
  N31: r140.pin3, Outputs.pin2
  N32: r140.pin4, Outputs.pin3
  N33: r140.pin5, Outputs.pin4
  N34: r140.pin6, Outputs.pin5
  N35: r140.pin7, Outputs.pin6
  N36: r140.pin8, Outputs.pin7
  N37: r140.pin9, Outputs.pin8

notes:
  0v
  1
  2
  3
  4
  5
  6
  7
  8
  Status
  5v
  Rx
  3v3
  A0
  A1
  A2
  A3
  A4
  A5
  Tx
  www.mccauslandcenter.sc.edu/CRNL/stimsync
